# Fritzing sketch ardunio_scanner_stepper (saved by Fritzing 0.8.7b)
breadboards: 1

parts:
  Part1 = Arduino Uno (Rev3)
  IC1 = H-Bridge [package=THT]
  S1 = Pushbutton [package="[THT]"]
  S2 = Pushbutton [package="[THT]"]
  LED1 = LED - 5mm [color="Blue (505nm)" package="5 mm [THT]"]
  R1 = Resistor [tolerance=±5% resistance=220 package=THT]
  R2 = Resistor [tolerance=±5% resistance=1k package=THT]
  M1 = Stepper Motor - Bipolar [part_number=STH-39d1126-02]
  R3 = Resistor [tolerance=±5% resistance=1k package=THT]
  VCC1 = 4 x AAA Battery Mount

nets:
  N1: Part1.D8, S1.Pin_3, S1.Pin_4, R3.Pin_0
  N2: Part1.D10_PWM/SS, LED1.anode
  N3: Part1.D12/MISO, S2.Pin_3, S2.Pin_4, R2.Pin_0
  N4: Part1.D2, IC1.2A
  N5: Part1.D3_PWM, IC1.1_2EN, IC1.3_4EN
  N6: Part1.D4, IC1.1A
  N7: Part1.D5_PWM, IC1.3A
  N8: Part1.D6_PWM, IC1.4A
  N9: Part1.5V, IC1.VCC1, S1.Pin_1, S1.Pin_2, S2.Pin_1, S2.Pin_2
  GND: Part1.GND, IC1.GND1, IC1.GND2, IC1.GND3, IC1.GND4, R1.Pin_1, R2.Pin_1, R3.Pin_1, VCC1.-
  N10: IC1.1Y, M1.A
  N11: IC1.2Y, M1.C
  N12: IC1.VCC2, VCC1.+
  N13: IC1.3Y, M1.B
  N14: IC1.4Y, M1.D
  N15: LED1.cathode, R1.Pin_0
